# Fritzing sketch lochrasterSensoren (saved by Fritzing 0.9.8b)
perfboards: 1

parts:
  M1 = BME280
  M2 = BME280
  Bauteil2 = Adafruit VL6180 Time of Flight Sensor [part_number="Adafruit #3316"]
  PololuVL6180X2 = VL6180X
  PololuVL6180X1 = VL6180X
  Bauteil1 = Adafruit VL6180 Time of Flight Sensor [part_number="Adafruit #3316"]
  R1 = Resistor [tolerance=±5% power=0.25 resistance=10000 package=THT]
  R2 = Resistor [tolerance=±5% power=0.25 resistance=10000 package=THT]
  R3 = Resistor [tolerance=±5% power=0.25 resistance=10000 package=THT]
  R4 = Resistor [tolerance=±5% power=0.25 resistance=10000 package=THT]
  J1 = Camdenboss CTB0158-6 [part_number=CTB0158-6 package=THT]
  J2 = Camdenboss CTB0158-2 [part_number=CTB0158-2 package=THT]
  Bauteil3 = Adafruit Feather M0 RFM9x LoRa [part_number="Adafruit #3178 or #3179"]  # not connected

nets:
  VIN: M1.VIN, M2.VIN, Bauteil2.VCC, J1.pin6
  GND: M1.GND, M2.GND, J1.pin5
  N1: M1.SCL, M2.SCL
  N2: M1.SDA, M2.SDA
  N3: Bauteil2.GPIO, R3.Pin_0, J1.pin2
  N4: PololuVL6180X2.GPIO0, R2.Pin_0, J1.pin1
  N5: PololuVL6180X2.VDD, R2.Pin_1, R3.Pin_1
  N6: PololuVL6180X1.GPIO0, R1.Pin_0, J1.pin3
  N7: PololuVL6180X1.VDD, R1.Pin_1, R4.Pin_1
  N8: Bauteil1.SDA, J2.pin1
  N9: Bauteil1.SCL, J2.pin2
  N10: Bauteil1.GPIO, R4.Pin_0, J1.pin4

notes:
  Microcontroller (uC)
  VL6180X #1
  (Pololu)
  VL6180X #2
  (Adafruit)
  VL6180X #3
  (Pololu)
  VL6180X #4
  (Adafruit)
  BME280 #1
  BME280 #2
  Perfboard

custom parts:
  BME280: Temperature Humidity Barometric presure Sensor
  Adafruit VL6180 Time of Flight Sensor: The VL6180X (sometimes called the VL6180) is a Time of Flight distance sensor like no other you've used! The sensor contains a very tiny laser source, and a matching sensor. The VL6180X can detect the "time of flight", or how long the laser light has taken to bounce back to the sensor. Since it uses a very narrow light source, it is good for determining distance of only the surface directly in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
  Adafruit Feather M0 RFM9x LoRa: This is the Adafruit Feather M0 RFM95 LoRa Radio - our take on an microcontroller with a "Long Range (LoRa)" packet radio transceiver with built in USB and battery charging. Its an Adafruit Feather M0 with a 433Mhz or 900MHz radio module cooked in! Great for making wireless networks that are more flexible than Bluetooth LE and without the high power requirements of WiFi. We have other boards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
