# Fritzing sketch wiring (saved by Fritzing 0.9.6b)
breadboards: 2

parts:
  Bauteil1 = Adafruit Feather M0 RFM9x LoRa [part_number="Adafruit #3178 or #3179"]
  Bauteil2 = Adafruit VL6180X Time of Flight Distance Sensor [part_number="Adafruit #3316"]
  Bauteil3 = Adafruit VL6180X Time of Flight Distance Sensor [part_number="Adafruit #3316"]
  Bauteil4 = Adafruit VL6180X Time of Flight Distance Sensor [part_number="Adafruit #3316"]
  Bauteil5 = Adafruit VL6180X Time of Flight Distance Sensor [part_number="Adafruit #3316"]
  Bauteil6 = Adafruit TCA9548A
  R1 = Resistor [tolerance=±5% power=0.25 resistance=4.7k package=THT]
  R2 = Resistor [tolerance=±5% power=0.25 resistance=4.7k package=THT]
  Bauteil7 = BME280 Breakout
  Bauteil8 = BME280 Breakout

nets:
  N1: Bauteil1.DIO1, Bauteil1.D6
  GND: Bauteil1.GND, Bauteil2.GND, Bauteil3.GND, Bauteil4.GND, Bauteil5.GND, Bauteil6.GND, Bauteil7.GND, Bauteil8.GND
  VIN: Bauteil1.+3V3, Bauteil2.VIN, Bauteil3.VIN, Bauteil4.VIN, Bauteil5.VIN, Bauteil6.VCC, R1.Pin_0, R2.Pin_0, Bauteil7.3.3V, Bauteil8.3.3V
  N2: Bauteil1.D12, Bauteil4.XSHUT
  N3: Bauteil1.D11, Bauteil2.XSHUT
  N4: Bauteil1.D10, Bauteil3.XSHUT
  N5: Bauteil1.D5, Bauteil5.XSHUT
  N6: Bauteil1.SCL, Bauteil2.SCL, Bauteil3.SCL, Bauteil4.SCL, Bauteil5.SCL, Bauteil6.INPUTSCL, R2.Pin_1
  N7: Bauteil1.SDA, Bauteil2.SDA, Bauteil3.SDA, Bauteil4.SDA, Bauteil5.SDA, Bauteil6.INPUTSDA, R1.Pin_1
  N8: Bauteil6.0SDA, Bauteil8.SDI/SDA
  N9: Bauteil6.0SCL, Bauteil8.SCK/SCL
  N10: Bauteil6.1SDA, Bauteil7.SDI/SDA
  N11: Bauteil6.1SCL, Bauteil7.SCK/SCL

custom parts:
  Adafruit Feather M0 RFM9x LoRa: This is the Adafruit Feather M0 RFM95 LoRa Radio - our take on an microcontroller with a "Long Range (LoRa)" packet radio transceiver with built in USB and battery charging. Its an Adafruit Feather M0 with a 433Mhz or 900MHz radio module cooked in! Great for making wireless networks that are more flexible than Bluetooth LE and without the high power requirements of WiFi. We have other boards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
  Adafruit VL6180X Time of Flight Distance Sensor: The VL6180X is a Time of Flight distance sensor like no other you've used! The sensor contains a very tiny invisible laser source, and a matching sensor. The VL6180X can detect the "time of flight", or how long the light has taken to bounce back to the sensor. Since it uses a very narrow light source, it is good for determining distance of only the surface directly in front of it. Unlike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
  Adafruit TCA9548A: You just found the perfect I2C sensor, and you want to wire up two or three or more of them to your Arduino when you realize "Uh oh, this chip has a fixed I2C address, and from what I know about I2C, you cannot have two devices with the same address on the same SDA/SCL pins!" Are you out of luck? You would be, if you didn't have this ultra-cool TCA9548A 1-to-8 I2C multiplexer! Finally, a way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
